// Logisim project Practica4.circ as structural Verilog
module XOR (
  input  P,
  input  Q,
  output P_XOR_Q
);

  wire and_1_out, and_2_out, not_1_out, not_2_out;

  not not_1 (not_1_out, P);
  not not_2 (not_2_out, Q);
  and and_1 (and_1_out, not_1_out, Q);
  and and_2 (and_2_out, P, not_2_out);
  or or_1 (P_XOR_Q, and_1_out, and_2_out);

  // Notes on the sheet:
  //   Compuerta XOR
endmodule

module convOp (
  input  [2:0] in,
  output [1:0] out
);

  wire and_1_out, and_2_out, and_3_out, and_4_out, not_1_out, not_2_out, not_3_out;

  not not_1 (not_1_out, in[2]);
  not not_2 (not_2_out, in[1]);
  not not_3 (not_3_out, in[0]);
  and and_1 (and_1_out, not_1_out, not_2_out, in[0]);
  and and_2 (and_2_out, in[2], in[1]);
  or or_1 (out[0], and_1_out, and_2_out, and_3_out);
  and and_3 (and_3_out, not_3_out, in[1]);
  and and_4 (and_4_out, in[1], in[0]);
  or or_2 (out[1], in[2], and_4_out);
endmodule

module convOut (
  input  [2:0] in,
  output out
);

  wire not_1_out;

  not not_1 (not_1_out, in[2]);
  and and_1 (out, in[0], in[1], not_1_out);
endmodule

module convA (
  input  [2:0] in,
  output out
);

  wire not_1_out, not_2_out;

  not not_1 (not_1_out, in[0]);
  not not_2 (not_2_out, in[2]);
  and and_1 (out, not_1_out, in[1], not_2_out);
endmodule

module convB (
  input  [2:0] in,
  output out
);

  wire and_1_out;

  and and_1 (and_1_out, in[0], in[2]);
  or or_1 (out, in[1], and_1_out);
endmodule

// ALU
module ALU_1_bit (
  input  Ci,
  input  [1:0] Op,
  input  e,
  input  A,
  input  B,
  output S,
  output Ci_1
);

  wire and_1_out, and_2_out, and_3_out, not_1_out, or_1_out, or_2_out, xor_1_p_xor_q, xor_2_p_xor_q;

  and and_1 (and_1_out, B, A);
  and and_2 (and_2_out, A, B);
  or or_1 (or_1_out, A, B);
  XOR xor_1 (.P(A), .Q(B), .P_XOR_Q(xor_1_p_xor_q));
  and and_3 (and_3_out, Ci, xor_1_p_xor_q);
  or or_2 (or_2_out, and_1_out, and_3_out);
  not not_1 (not_1_out, Op[0]);
  and and_4 (Ci_1, or_2_out, not_1_out, Op[1]);
  XOR xor_2 (.P(Ci), .Q(xor_1_p_xor_q), .P_XOR_Q(xor_2_p_xor_q));
  Multiplexer #(.select(2)) multiplexer_1 (
    .in0(and_2_out), .in1(or_1_out), .in2(xor_2_p_xor_q), .out(S), .sel(Op), .en(e));  // open: in3

  // Notes on the sheet:
  //   ALU de 1 bit
endmodule

// ALU8
module ALU_8_bits (
  input  [1:0] Op,
  input  C0,
  input  e,
  input  [7:0] A,
  input  [7:0] B,
  output [7:0] A_op_B,
  output Desbordamiento
);

  wire alu_1_bit_1_ci_1, alu_1_bit_2_ci_1, alu_1_bit_3_ci_1, alu_1_bit_4_ci_1, alu_1_bit_5_ci_1,
       alu_1_bit_6_ci_1, alu_1_bit_7_ci_1;

  ALU_1_bit alu_1_bit_1 (.A(A[0]), .B(B[0]), .S(A_op_B[0]), .Ci(C0), .Op(Op), .Ci_1(alu_1_bit_1_ci_1), .e(e));
  ALU_1_bit alu_1_bit_2 (
    .A(A[1]), .B(B[1]), .S(A_op_B[1]), .Ci(alu_1_bit_1_ci_1), .Op(Op), .Ci_1(alu_1_bit_2_ci_1), .e(e));
  ALU_1_bit alu_1_bit_3 (
    .A(A[2]), .B(B[2]), .S(A_op_B[2]), .Ci(alu_1_bit_2_ci_1), .Op(Op), .Ci_1(alu_1_bit_3_ci_1), .e(e));
  ALU_1_bit alu_1_bit_4 (
    .A(A[3]), .B(B[3]), .S(A_op_B[3]), .Ci(alu_1_bit_3_ci_1), .Op(Op), .Ci_1(alu_1_bit_4_ci_1), .e(e));
  ALU_1_bit alu_1_bit_5 (
    .A(A[4]), .B(B[4]), .S(A_op_B[4]), .Ci(alu_1_bit_4_ci_1), .Op(Op), .Ci_1(alu_1_bit_5_ci_1), .e(e));
  ALU_1_bit alu_1_bit_6 (
    .A(A[5]), .B(B[5]), .S(A_op_B[5]), .Ci(alu_1_bit_5_ci_1), .Op(Op), .Ci_1(alu_1_bit_6_ci_1), .e(e));
  ALU_1_bit alu_1_bit_7 (
    .A(A[6]), .B(B[6]), .S(A_op_B[6]), .Ci(alu_1_bit_6_ci_1), .Op(Op), .Ci_1(alu_1_bit_7_ci_1), .e(e));
  ALU_1_bit alu_1_bit_8 (
    .A(A[7]), .B(B[7]), .S(A_op_B[7]), .Ci(alu_1_bit_7_ci_1), .Op(Op), .Ci_1(Desbordamiento), .e(e));

  // Notes on the sheet:
  //   ALU de 8 bits
endmodule

// -
module resta (
  input  [7:0] A,
  input  [7:0] B,
  output [7:0] A_B
);

  wire [7:0] not_1_out;

  assign not_1_out = ~B;  // NOT_Gate not_1, 8 bits wide
  ALU_8_bits alu_8_bits_1 (
    .Op(2'b10), .A(A), .B(not_1_out), .A_op_B(A_B), .C0(1'b1), .e(1'b1));  // open: Desbordamiento
endmodule

// -
module igualdad (
  input  [7:0] A,
  input  [7:0] B,
  output [7:0] A____B
);

  wire [7:0] resta_1_a_b;

  resta resta_1 (.A(A), .B(B), .A_B(resta_1_a_b));
  assign A____B = ~resta_1_a_b;  // NOT_Gate not_1, 8 bits wide
endmodule

module NOR (
  input  [7:0] in_1,
  input  [7:0] in_2,
  output [7:0] out_3
);

  wire [7:0] not_1_out, not_2_out;

  assign not_1_out = ~in_1;  // NOT_Gate not_1, 8 bits wide
  assign not_2_out = ~in_2;  // NOT_Gate not_2, 8 bits wide
  ALU_8_bits alu_8_bits_1 (
    .Op(2'b00), .A(not_1_out), .B(not_2_out), .A_op_B(out_3), .C0(1'b0), .e(1'b1));  // open: Desbordamiento
endmodule

module ALU_full (
  input  [2:0] Op,
  input  e,
  input  [7:0] A,
  input  [7:0] B,
  output [7:0] A_Op_B
);

  wire conva_1_out, convb_1_out, convcarry_1_out, convout_1_out;
  wire [1:0] convop_1_out;
  wire [7:0] alu_8_bits_1_a_op_b, multiplexer_1_out, multiplexer_2_out, not_1_out, not_2_out, not_3_out;

  assign not_1_out = ~A;  // NOT_Gate not_1, 8 bits wide
  convA conva_1 (.in(Op), .out(conva_1_out));
  Multiplexer #(.width(8)) multiplexer_1 (
    .in0(A), .in1(not_1_out), .out(multiplexer_1_out), .sel(conva_1_out), .en(1'b1));
  convB convb_1 (.in(Op), .out(convb_1_out));
  Multiplexer #(.width(8)) multiplexer_2 (
    .in0(B), .in1(not_2_out), .out(multiplexer_2_out), .sel(convb_1_out), .en(1'b1));
  assign not_2_out = ~B;  // NOT_Gate not_2, 8 bits wide
  convCarry convcarry_1 (.in(Op), .out(convcarry_1_out));
  convOp convop_1 (.in(Op), .out(convop_1_out));
  ALU_8_bits alu_8_bits_1 (
    .Op(convop_1_out), .A(multiplexer_1_out), .B(multiplexer_2_out), .A_op_B(alu_8_bits_1_a_op_b),
    .C0(convcarry_1_out), .e(e));  // open: Desbordamiento
  convOut convout_1 (.in(Op), .out(convout_1_out));
  Multiplexer #(.width(8)) multiplexer_3 (
    .in0(alu_8_bits_1_a_op_b), .in1(not_3_out), .out(A_Op_B), .sel(convout_1_out), .en(1'b1));
  assign not_3_out = ~alu_8_bits_1_a_op_b;  // NOT_Gate not_3, 8 bits wide
endmodule

module convCarry (
  input  [2:0] in,
  output out
);

  wire not_1_out;

  not not_1 (not_1_out, in[1]);
  and and_1 (out, in[0], not_1_out, in[2]);
endmodule
